# Fritzing sketch PiClockRgbLeds (saved by Fritzing 0.8.7b)
circuit board: 16cm x 10cm
breadboards: 3

parts:
  SR2 = Mystery Part - 16 pins [chip_label=SN74HC595 package=THT]
  A = Arduino Uno (Rev3)
  SR1 = Mystery Part - 16 pins [chip_label=SN74HC595 package=THT]
  LED1 = RGB LED (com. cathode, rbg) [package="5 mm [THT]"]
  LED2 = RGB LED (com. cathode, rbg) [package="5 mm [THT]"]
  LED3 = RGB LED (com. cathode, rbg) [package="5 mm [THT]"]
  LED4 = RGB LED (com. cathode, rbg) [package="5 mm [THT]"]
  LED5 = RGB LED (com. cathode, rbg) [package="5 mm [THT]"]
  LED6 = RGB LED (com. cathode, rbg) [package="5 mm [THT]"]
  LED8 = RGB LED (com. cathode, rbg) [package="5 mm [THT]"]
  LED7 = RGB LED (com. cathode, rbg) [package="5 mm [THT]"]
  LED9 = RGB LED (com. cathode, rbg) [package="5 mm [THT]"]
  RB5 = Resistor [tolerance=±5% resistance=1k package=THT]
  RG6 = Resistor [tolerance=±5% resistance=3.3k package=THT]
  RR1 = Resistor [tolerance=±5% resistance=1k package=THT]
  RR2 = Resistor [tolerance=±5% resistance=1k package=THT]
  RR3 = Resistor [tolerance=±5% resistance=1k package=THT]
  RR4 = Resistor [tolerance=±5% resistance=1k package=THT]
  RR5 = Resistor [tolerance=±5% resistance=1k package=THT]
  RR6 = Resistor [tolerance=±5% resistance=1k package=THT]
  RG1 = Resistor [tolerance=±5% resistance=3.3k package=THT]
  RG2 = Resistor [tolerance=±5% resistance=3.3k package=THT]
  RG3 = Resistor [tolerance=±5% resistance=3.3k package=THT]
  RG4 = Resistor [tolerance=±5% resistance=3.3k package=THT]
  RG5 = Resistor [tolerance=±5% resistance=3.3k package=THT]
  RB1 = Resistor [tolerance=±5% resistance=1k package=THT]
  RB2 = Resistor [tolerance=±5% resistance=1k package=THT]
  RB3 = Resistor [tolerance=±5% resistance=1k package=THT]
  RB4 = Resistor [tolerance=±5% resistance=1k package=THT]
  RSR = Resistor [tolerance=±5% resistance=10k package=THT]
  RT1H = Resistor [tolerance=±5% resistance=1M package=THT]
  TR = Resistor [tolerance=±5% resistance=0 package=THT]
  TL = Resistor [tolerance=±5% resistance=0 package=THT]
  RT2H = Resistor [tolerance=±5% resistance=1M package=THT]
  RT1S = Resistor [tolerance=±5% resistance=1k package=THT]
  RT2S = Resistor [tolerance=±5% resistance=1k package=THT]

nets:
  N1: SR2.pin1, RG4.Pin_0
  N2: SR2.pin2, RG5.Pin_0
  N3: SR2.pin3, RG6.Pin_0
  N4: SR2.pin4, RB1.Pin_0
  N5: SR2.pin5, RB2.Pin_0
  N6: SR2.pin6, RB3.Pin_0
  N7: SR2.pin7, RB4.Pin_0
  N8: SR2.pin8, SR2.pin13, A.GND, SR1.pin8, SR1.pin13, LED1.common_cathode, LED2.common_cathode, LED3.common_cathode, LED4.common_cathode, LED5.common_cathode, LED6.common_cathode, LED8.common_cathode, LED7.common_cathode, LED9.common_cathode, RSR.Pin_1
  N9: SR2.pin10, SR2.pin16, A.5V, SR1.pin10, SR1.pin16
  N10: SR2.pin11, A.D4, SR1.pin11
  N11: SR2.pin12, A.D3_PWM, SR1.pin12
  N12: SR2.pin14, SR1.pin9
  N13: SR2.pin15, RG3.Pin_0
  N14: A.D8, RT1H.Pin_0, RT1S.Pin_1
  N15: A.D9_PWM, RT1H.Pin_1
  N16: A.D10_PWM/SS, RT2H.Pin_0, RT2S.Pin_1
  N17: A.D11_PWM/MOSI, RT2H.Pin_1
  N18: A.D2, SR1.pin14, RSR.Pin_0
  N19: A.D5_PWM, RB5.Pin_0
  N20: SR1.pin1, RR2.Pin_0
  N21: SR1.pin2, RR3.Pin_0
  N22: SR1.pin3, RR4.Pin_0
  N23: SR1.pin4, RR5.Pin_0
  N24: SR1.pin5, RR6.Pin_0
  N25: SR1.pin6, RG1.Pin_0
  N26: SR1.pin7, RG2.Pin_0
  N27: SR1.pin15, RR1.Pin_0
  N28: LED1.red_anode, RR1.Pin_1
  N29: LED1.blue_anode, RB4.Pin_1
  N30: LED2.red_anode, RR2.Pin_1
  N31: LED2.blue_anode, RB5.Pin_1
  N32: LED3.red_anode, RR3.Pin_1
  N33: LED4.red_anode, RR4.Pin_1
  N34: LED4.green_anode, RG1.Pin_1
  N35: LED5.red_anode, RR5.Pin_1
  N36: LED5.green_anode, RG2.Pin_1
  N37: LED6.red_anode, RR6.Pin_1
  N38: LED6.green_anode, RG3.Pin_1
  N39: LED8.blue_anode, RB2.Pin_1
  N40: LED8.green_anode, RG5.Pin_1
  N41: LED7.blue_anode, RB1.Pin_1
  N42: LED7.green_anode, RG4.Pin_1
  N43: LED9.blue_anode, RB3.Pin_1
  N44: LED9.green_anode, RG6.Pin_1
  N45: TR.Pin_0, RT2S.Pin_0
  N46: TL.Pin_0, RT1S.Pin_0

notes:
  SN74HC595
  16 15 14 13 12 11 10 9
  | | | | | | | |
  +--+--+--+--+--+--+--+
  |> |
  +--+--+--+--+--+--+--+
  | | | | | | | |
  1 2 3 4 5 6 7 8
  Officiele pin namen:
  1: Q2
  2: Q3
  3: Q4
  3: Q5
  5: Q6
  6: Q7
  7: Q8
  8: GND
  9: QH* (voor daisy chaining)
  10: SRCLR* (naar 5V)
  11: SRCLK (naar D4): clock pin
  12: RCLK (naar D3): latch pin
  13: OE* (naar GND)
  14: SER (naar D2): data pin
  15: Q1
  16: VCC (naar 5V)
  SN74HC595
  16 15 14 13 12 11 10 9
  | | | | | | | |
  +--+--+--+--+--+--+--+
  |> |
  +--+--+--+--+--+--+--+
  | | | | | | | |
  1 2 3 4 5 6 7 8
  Verbindingen:
  1: LED 2
  2: LED 3
  3: LED 4
  3: LED 5
  5: LED 6
  6: LED 7
  7: LED 8
  8: GND
  9: daisy chaining
  10: naar 5V
  11: naar D4: clock pin
  12: naar D3: latch pin
  13: naar GND
  14: naar D2: data pin
  15: naar LED1
  16: naar 5V
  const int datapin = 2;
  const int latchpin = 3;
  const int clockpin = 4;
  void setup()
  {
  pinMode(datapin, OUTPUT);
  pinMode(latchpin, OUTPUT);
  pinMode(clockpin, OUTPUT);
  }
  void loop()
  {
  for (byte i=0; i!=256; ++i)
  {
  //Laat het getal i als binair zien
  ShowBinary(i);
  delay(100);
  }
  }
  void ShowBinary(const byte getal)
  {
  // Stuur de data naar het shift register
  shiftOut(datapin, clockpin, MSBFIRST, getal);
  // Zet de latch aan en uit, zodat de outputs aan gaan
  digitalWrite(latchpin, HIGH);
  digitalWrite(latchpin, LOW);
  }
  Blue = 2 = data = SER of SN74HC595
  Yellow = 3 = latch = RCLK of SN74HC595
  Green = 4 = clock = SRCLK of SN74HC595
  Orange = daisy chain
  White = 16 hours pin
  R_SR: Pull-down resistance for shift register, ensures all lights sty off when machine is turned on

custom parts:
  Mystery Part - 16 pins: A dummy, proxy, ersatz, stand-in part for whatever you want. With 16 pins on a 300mil inline pin header footprint.
