# Fritzing sketch PiClockRgbLedsStandalone (saved by Fritzing 0.8.7b)
circuit board: 16cm x 10cm
breadboards: 4

parts:
  SR2 = Mystery Part - 16 pins [chip_label=SN74HC595 package=THT]
  SR1 = Mystery Part - 16 pins [chip_label=SN74HC595 package=THT]
  LED1 = RGB LED (com. cathode, rbg) [package="5 mm [THT]"]
  LED2 = RGB LED (com. cathode, rbg) [package="5 mm [THT]"]
  LED3 = RGB LED (com. cathode, rbg) [package="5 mm [THT]"]
  LED4 = RGB LED (com. cathode, rbg) [package="5 mm [THT]"]
  LED5 = RGB LED (com. cathode, rbg) [package="5 mm [THT]"]
  LED6 = RGB LED (com. cathode, rbg) [package="5 mm [THT]"]
  LED8 = RGB LED (com. cathode, rbg) [package="5 mm [THT]"]
  LED7 = RGB LED (com. cathode, rbg) [package="5 mm [THT]"]
  LED9 = RGB LED (com. cathode, rbg) [package="5 mm [THT]"]
  RB5 = Resistor [tolerance=±5% resistance=1k package=THT]
  RG6 = Resistor [tolerance=±5% resistance=3.3k package=THT]
  RR1 = Resistor [tolerance=±5% resistance=1k package=THT]
  RR2 = Resistor [tolerance=±5% resistance=1k package=THT]
  RR3 = Resistor [tolerance=±5% resistance=1k package=THT]
  RR4 = Resistor [tolerance=±5% resistance=1k package=THT]
  RR5 = Resistor [tolerance=±5% resistance=1k package=THT]
  RR6 = Resistor [tolerance=±5% resistance=1k package=THT]
  RG1 = Resistor [tolerance=±5% resistance=3.3k package=THT]
  RG2 = Resistor [tolerance=±5% resistance=3.3k package=THT]
  RG3 = Resistor [tolerance=±5% resistance=3.3k package=THT]
  RG4 = Resistor [tolerance=±5% resistance=3.3k package=THT]
  RG5 = Resistor [tolerance=±5% resistance=3.3k package=THT]
  RB1 = Resistor [tolerance=±5% resistance=1k package=THT]
  RB2 = Resistor [tolerance=±5% resistance=1k package=THT]
  RB3 = Resistor [tolerance=±5% resistance=1k package=THT]
  RB4 = Resistor [tolerance=±5% resistance=1k package=THT]
  VCC1 = 4 x AAA Battery Mount
  A1 = atmega328 [package=dip]
  C2 = Capacitor [package=cap-pth-small2]
  C1 = Capacitor [package=cap-pth-small2]
  Y1 = CRYSTAL [package=crystal-smd-10.5x4.8-2pin]
  RT2H = Resistor [tolerance=±5% resistance=1M package=THT]
  RT1H = Resistor [tolerance=±5% resistance=1M package=THT]
  RSR = Resistor [tolerance=±5% resistance=10k package=THT]
  RT1S = Resistor [tolerance=±5% resistance=1k package=THT]
  TL = Resistor [tolerance=±5% resistance=0 package=THT]
  TR = Resistor [tolerance=±5% resistance=0 package=THT]
  RT2S = Resistor [tolerance=±5% resistance=1k package=THT]
  RRST = Resistor [tolerance=±5% resistance=10k package=THT]
  BEEP = Piezo Speaker
  J5V = female pin header, 2 pins [form="♀ (female)"]

nets:
  N1: SR2.pin1, RG4.Pin_0
  N2: SR2.pin2, RG5.Pin_0
  N3: SR2.pin3, RG6.Pin_0
  N4: SR2.pin4, RB1.Pin_0
  N5: SR2.pin5, RB2.Pin_0
  N6: SR2.pin6, RB3.Pin_0
  N7: SR2.pin7, RB4.Pin_0
  N8: SR2.pin8, SR2.pin13, SR1.pin8, SR1.pin13, LED1.common_cathode, LED2.common_cathode, LED3.common_cathode, LED4.common_cathode, LED5.common_cathode, LED6.common_cathode, LED8.common_cathode, LED7.common_cathode, LED9.common_cathode, VCC1.-, A1.GND, C2.2, C1.2, RSR.Pin_1, RRST.Pin_1, BEEP.pin1, J5V.pin1
  N9: SR2.pin10, SR2.pin16, SR1.pin10, SR1.pin16, VCC1.+, A1.RESET, A1.VCC, A1.D7, A1.AVCC, A1.AREF, RRST.Pin_0, J5V.pin2
  N10: SR2.pin11, SR1.pin11, A1.D4
  N11: SR2.pin12, SR1.pin12, A1.D3_(PWM)
  N12: SR2.pin14, SR1.pin9
  N13: SR2.pin15, RG3.Pin_0
  N14: SR1.pin1, RR2.Pin_0
  N15: SR1.pin2, RR3.Pin_0
  N16: SR1.pin3, RR4.Pin_0
  N17: SR1.pin4, RR5.Pin_0
  N18: SR1.pin5, RR6.Pin_0
  N19: SR1.pin6, RG1.Pin_0
  N20: SR1.pin7, RG2.Pin_0
  N21: SR1.pin14, A1.D2, RSR.Pin_0
  N22: SR1.pin15, RR1.Pin_0
  N23: LED1.red_anode, RR1.Pin_1
  N24: LED1.blue_anode, RB4.Pin_1
  N25: LED2.red_anode, RR2.Pin_1
  N26: LED2.blue_anode, RB5.Pin_1
  N27: LED3.red_anode, RR3.Pin_1
  N28: LED4.red_anode, RR4.Pin_1
  N29: LED4.green_anode, RG1.Pin_1
  N30: LED5.red_anode, RR5.Pin_1
  N31: LED5.green_anode, RG2.Pin_1
  N32: LED6.red_anode, RR6.Pin_1
  N33: LED6.green_anode, RG3.Pin_1
  N34: LED8.blue_anode, RB2.Pin_1
  N35: LED8.green_anode, RG5.Pin_1
  N36: LED7.blue_anode, RB1.Pin_1
  N37: LED7.green_anode, RG4.Pin_1
  N38: LED9.blue_anode, RB3.Pin_1
  N39: LED9.green_anode, RG6.Pin_1
  N40: RB5.Pin_0, A1.D5_(PWM)
  N41: A1.XLAT1, C1.1, Y1.1
  N42: A1.XLAT2, C2.1, Y1.2
  N43: A1.D6_(PWM), BEEP.pin2
  N44: A1.D8, RT1H.Pin_0, RT1S.Pin_1
  N45: A1.D9_(PWM), RT1H.Pin_1
  N46: A1.D10_(PWM), RT2H.Pin_0, RT2S.Pin_1
  N47: A1.D11_(PWM), RT2H.Pin_1
  N48: RT1S.Pin_0, TL.Pin_0
  N49: TR.Pin_0, RT2S.Pin_0

notes:
  SN74HC595
  16 15 14 13 12 11 10 9
  | | | | | | | |
  +--+--+--+--+--+--+--+
  |> |
  +--+--+--+--+--+--+--+
  | | | | | | | |
  1 2 3 4 5 6 7 8
  Officiele pin namen:
  1: Q2
  2: Q3
  3: Q4
  3: Q5
  5: Q6
  6: Q7
  7: Q8
  8: GND
  9: QH* (voor daisy chaining)
  10: SRCLR* (naar 5V)
  11: SRCLK (naar D4): clock pin
  12: RCLK (naar D3): latch pin
  13: OE* (naar GND)
  14: SER (naar D2): data pin
  15: Q1
  16: VCC (naar 5V)
  Blue = 2 = data = SER of SN74HC595
  Yellow = 3 = latch = RCLK of SN74HC595
  Green = 4 = clock = SRCLK of SN74HC595
  Orange = daisy chain
  White = 16 hours pin
  Capacitors: 22 pF
  Crystal: 16 MHz
  RSR: Pull-down resistance for shift register, ensures all lights sty off when machine is turned on
  RRST: Pull-up resistance for reset

custom parts:
  Mystery Part - 16 pins: A dummy, proxy, ersatz, stand-in part for whatever you want. With 16 pins on a 300mil inline pin header footprint.
